# Fritzing sketch smart_home_wiring (saved by Fritzing 0.9.3b)

parts:
  U1 = ESP8266 NodeMCU LoLin module
  U2 = Module 4 Relais 5V [package="Module 4 Relais 5V"]

nets:
  N1: U1.D1, U2.IN1
  N2: U1.D2, U2.IN2
  N3: U1.D3, U2.IN3
  N4: U1.D4, U2.IN4
  3V3: U1.3V3, U2.VCC
  GND: U1.GND, U2.GND

custom parts:
  ESP8266 NodeMCU LoLin module: ESP8266 based NodeMCU
  Module 4 Relais 5V: Module 4 Relais 5V 4x SPD-06VDC-SD-C
