# Fritzing sketch smart_lock_wiring (saved by Fritzing 0.9.3b)

parts:
  U1 = ESP8266 NodeMCU LoLin module
  Part1 = RFID-RC522-v2
  OLED_I2C1 = OLED 128x64 I2C Monochrome Display
  M1 = 1 chan 5v relay module

nets:
  N1: U1.D1, Part1.RST, OLED_I2C1.SCK
  N2: U1.D2, Part1.SDA, OLED_I2C1.SDA
  3V3: U1.3V3, Part1.3.3V, OLED_I2C1.VDD, M1.pin_1
  GND: U1.GND, Part1.GND, OLED_I2C1.GND, M1.pin_2
  N3: U1.D5, Part1.SCK, M1.pin_3
  N4: U1.D6, Part1.MISO
  N5: U1.D7, Part1.MOSI

custom parts:
  ESP8266 NodeMCU LoLin module: ESP8266 based NodeMCU
  RFID-RC522-v2: A simple China made RFID-RC522 Reader; do check the pin labels, as this is a MFRC522 based clone.
  1 chan 5v relay module: 1 Channel 5V Relay Module Board Shield with Optocoupler Support High and Low Level Trigger for Arduino.
